# Fritzing sketch PCV (saved by Fritzing 0.9.3b)
breadboards: 2

parts:
  Part1 = Arduino Nano (Rev3.0) (ICSP)
  J1 = Basic Force Sensing Resistor (FSR) [package=THT]
  R1 = Resistor [tolerance=±5% resistance=10k package="0603 [SMD]"]
  LED1 = LED - 3mm [color="Red (633nm)" package="3 mm [THT]"]
  Raspberry_Pi_1 = Raspberry Pi 3 [part_number=RPI-3-V1.2]
  LCM1602_IIC1 = LCM1602 IIC [part_number="LCM1602 IIC" chip_label="LCM1602 IIC" package="DIP (Dual Inline) [THT]"]
  U1 = LCD-16X2 [package=lcd-16x2]
  Part2 = RFID-RC522-v2
  CAMERA1 = TTL Serial JPEG Camera  # not connected

nets:
  N1: Part1.GND, J1.pin_1, R1.Pin_0
  N2: Part1.D3, LED1.anode
  N3: Part1.A0, J1.pin_0, R1.Pin_1
  N4: Raspberry_Pi_1.3v3, LCM1602_IIC1.LED_A, Part2.3_3V
  N5: Raspberry_Pi_1.GPIO2, LCM1602_IIC1.SDA
  N6: Raspberry_Pi_1.GPIO3, LCM1602_IIC1.SCL
  N7: Raspberry_Pi_1.GPIO10, Part2.MOSI
  N8: Raspberry_Pi_1.GPIO9, Part2.MISO
  N9: Raspberry_Pi_1.GPIO11, Part2.SCK
  N10: Raspberry_Pi_1.GPIO8, Part2.SDA
  N11: Raspberry_Pi_1.GPIO25, Part2.RST
  5V: Raspberry_Pi_1.5V, LCM1602_IIC1.VCC
  VSS: LCM1602_IIC1.VSS, U1.VSS
  VDD: LCM1602_IIC1.VDD, U1.VDD
  N12: LCM1602_IIC1.V0, U1.VO
  N13: LCM1602_IIC1.RS, U1.RS
  N14: LCM1602_IIC1.RW, U1.R_W
  N15: LCM1602_IIC1.E, U1.E
  N16: LCM1602_IIC1.D0, U1.DB0
  N17: LCM1602_IIC1.D1, U1.DB1
  N18: LCM1602_IIC1.D2, U1.DB2
  N19: LCM1602_IIC1.D3, U1.DB3
  N20: LCM1602_IIC1.D4, U1.DB4
  N21: LCM1602_IIC1.D5, U1.DB5
  N22: LCM1602_IIC1.D6, U1.DB6
  N23: LCM1602_IIC1.D7, U1.DB7
  N24: LCM1602_IIC1.A, U1.A
  N25: LCM1602_IIC1.K, U1.K
  GND: LCM1602_IIC1.GND, Part2.GND

custom parts:
  LCM1602 IIC: I2C-Module to use a 1602 or 2004 LCD on with the wire.h libory Serial LCD Modul
  RFID-RC522-v2: A simple China made RFID-RC522 Reader; do check the pin labels, as this is a MFRC522 based clone.
  TTL Serial JPEG Camera: TTL Serial JPEG Camera with NTSC Out
